// Logisim project encoder.circ as structural Verilog: 1 circuit, main circuit main
module main (
  input  in_1,
  input  in_2,
  input  in_3,
  input  in_4,
  input  in_5,
  input  in_6,
  input  in_7,
  input  in_8
);

  wire or_1_out, or_2_out, or_3_out;

  or or_1 (or_1_out, in_8, in_7, in_6, in_5);
  or or_2 (or_2_out, in_3, in_4, in_7, in_8);
  or or_3 (or_3_out, in_2, in_4, in_6, in_8);
  LED led_1 (.in(or_1_out));
  LED led_2 (.in(or_2_out));
  LED led_3 (.in(or_3_out));
endmodule
